# Fritzing sketch original_synth (saved by Fritzing 0.9.3b)
breadboards: 2

parts:
  Part1 = Arduino Uno (Rev3)  # not connected
  S1 = Pushbutton [package="[THT]"]
  LED1 = LED - 5mm [color="Red (633nm)" package="5 mm [THT]"]
  S2 = Pushbutton [package="[THT]"]
  R2 = Resistor [tolerance=±5% resistance=220 package=THT]
  LED2 = LED - 5mm [color="Red (633nm)" package="5 mm [THT]"]
  S3 = Pushbutton [package="[THT]"]
  LED3 = LED - 5mm [color="Red (633nm)" package="5 mm [THT]"]
  S4 = Pushbutton [package="[THT]"]
  LED4 = LED - 5mm [color="Red (633nm)" package="5 mm [THT]"]
  S5 = Pushbutton [package="[THT]"]
  LED5 = LED - 5mm [color="Red (633nm)" package="5 mm [THT]"]
  S6 = Pushbutton [package="[THT]"]
  LED6 = LED - 5mm [color="Red (633nm)" package="5 mm [THT]"]
  S7 = Pushbutton [package="[THT]"]
  LED7 = LED - 5mm [color="Red (633nm)" package="5 mm [THT]"]
  S8 = Pushbutton [package="[THT]"]
  LED8 = LED - 5mm [color="Red (633nm)" package="5 mm [THT]"]
  R9 = Resistor [tolerance=±5% resistance=220 package=THT]
  R10 = Resistor [tolerance=±5% resistance=220 package=THT]
  R11 = Resistor [tolerance=±5% resistance=220 package=THT]
  R12 = Resistor [tolerance=±5% resistance=220 package=THT]
  R13 = Resistor [tolerance=±5% resistance=220 package=THT]
  R14 = Resistor [tolerance=±5% resistance=220 package=THT]
  R15 = Resistor [tolerance=±5% resistance=220 package=THT]
  R16 = Resistor [tolerance=±5% resistance=220 package=THT]
  R17 = Resistor [tolerance=±5% resistance=220 package=THT]
  R18 = Resistor [tolerance=±5% resistance=220 package=THT]
  R19 = Resistor [tolerance=±5% resistance=220 package=THT]
  C1 = Tantalum Capacitor [capacitance=1nF package="A 3216 [SMD, tantalum]"]
  Part2 = Thumb Joystick  # not connected

nets:
  N1: S1.Pin_1, S1.Pin_2, LED1.anode
  N2: S1.Pin_3, S1.Pin_4, S3.Pin_3, S3.Pin_4, S4.Pin_3, S4.Pin_4, S5.Pin_3, S5.Pin_4, S6.Pin_3, S6.Pin_4, S7.Pin_3, S7.Pin_4
  N3: LED1.cathode, R9.Pin_1
  N4: S2.Pin_1, S2.Pin_2, LED2.anode
  N5: S2.Pin_3, S2.Pin_4
  N6: R2.Pin_0, R9.Pin_0, R10.Pin_0, R11.Pin_0, R12.Pin_0, R13.Pin_0, R14.Pin_0, R15.Pin_0
  N7: R2.Pin_1, LED2.cathode
  N8: S3.Pin_1, S3.Pin_2, LED3.anode
  N9: LED3.cathode, R10.Pin_1
  N10: S4.Pin_1, S4.Pin_2, LED4.anode
  N11: LED4.cathode, R11.Pin_1
  N12: S5.Pin_1, S5.Pin_2, LED5.anode
  N13: LED5.cathode, R12.Pin_1
  N14: S6.Pin_1, S6.Pin_2, LED6.anode
  N15: LED6.cathode, R13.Pin_1
  N16: S7.Pin_1, S7.Pin_2, LED7.anode
  N17: LED7.cathode, R14.Pin_1
  N18: S8.Pin_1, S8.Pin_2, LED8.anode
  N19: S8.Pin_3, S8.Pin_4
  N20: LED8.cathode, R15.Pin_1
  N21: R16.Pin_0, R17.Pin_0, R19.Pin_0, C1.+
  N22: R16.Pin_1, R17.Pin_1
  N23: R18.Pin_1, R19.Pin_1
